// Logisim project 5-digit-password.circ as structural Verilog: 13 circuits, main circuit main
module main (
);

  wire _0_out, _1_out, _2_out, _3_out, _4_out, _5_out, _6_out, _7_out, _8_out, _9_out, button_1_out,
       button_2_out, cccccooo_1_a, cccccooo_1_b, cccccooo_1_c_2, counterds_1_a, counterds_1_b, counterds_1_c,
       counterds_1_d, counterds_1_e, counterds_1_f, counterds_1_g, Decoder_a, Decoder_b, Decoder_c,
       Decoder_d, Decoder_e, Decoder_f, Decoder_g, encoderwithcontroler_1_w, encoderwithcontroler_1_x,
       encoderwithcontroler_1_y, encoderwithcontroler_1_z, M_out, mood_1_chk, mood_1_clk, mood_1_offled,
       mood_1_on_led, mood_1_sled, not_1_out;

  Button _1 (.out(_1_out));
  Button _2 (.out(_2_out));
  Button _4 (.out(_4_out));
  Button _5 (.out(_5_out));
  Button _8 (.out(_8_out));
  Button _7 (.out(_7_out));
  Button _0 (.out(_0_out));
  Button M (.out(M_out));
  Button _3 (.out(_3_out));
  Button _6 (.out(_6_out));
  Button _9 (.out(_9_out));
  Button button_1 (.out(button_1_out));
  Button button_2 (.out(button_2_out));
  encoderwithcontroler encoderwithcontroler_1 (
    ._0(_0_out), ._1(_1_out), ._2(_2_out), ._3(_3_out), ._4(_4_out), ._5(_5_out), ._6(_6_out), ._7(_7_out),
    ._8(_8_out), ._9(_9_out), .W(encoderwithcontroler_1_w), .X(encoderwithcontroler_1_x),
    .Y(encoderwithcontroler_1_y), .Z(encoderwithcontroler_1_z));
  decoder Decoder (
    .w(encoderwithcontroler_1_w), .x(encoderwithcontroler_1_x), .y(encoderwithcontroler_1_y),
    .z(encoderwithcontroler_1_z), .A(Decoder_a), .B(Decoder_b), .C(Decoder_c), .D(Decoder_d), .E(Decoder_e),
    .F(Decoder_f), .G(Decoder_g));
  mood mood_1 (
    .w(encoderwithcontroler_1_w), .x(encoderwithcontroler_1_x), .y(encoderwithcontroler_1_y),
    .z(encoderwithcontroler_1_z), .Mood(M_out), .clr(button_1_out), .Set(button_2_out), .chk(mood_1_chk),
    .clk(mood_1_clk), .Sled(mood_1_sled), .OFFLED(mood_1_offled), .ON_LED(mood_1_on_led));
  _7_Segment_Display u_7_segment_display_1 (
    .g(Decoder_g), .f(Decoder_f), .a(Decoder_a), .b(Decoder_b), .e(Decoder_e), .d(Decoder_d), .c(Decoder_c));  // open: dp
  LED led_1 (.in(mood_1_chk));
  not not_1 (not_1_out, mood_1_chk);
  _7_Segment_Display u_7_segment_display_2 (
    .g(mood_1_chk), .f(mood_1_chk), .a(mood_1_chk), .b(not_1_out), .c(not_1_out));  // open: e, d, dp
  LED led_2 (.in(mood_1_on_led));
  cccccooo cccccooo_1 (
    .A(cccccooo_1_a), .B(cccccooo_1_b), .C_2(cccccooo_1_c_2), .C(mood_1_clk), .R(button_1_out),
    .in_3(mood_1_sled));
  LED led_3 (.in(mood_1_offled));
  LED led_4 (.in(mood_1_sled));
  counterDs counterds_1 (
    .in_1(cccccooo_1_a), .Y(cccccooo_1_b), .Z(cccccooo_1_c_2), .a(counterds_1_a), .b(counterds_1_b),
    .c(counterds_1_c), .d(counterds_1_d), .e(counterds_1_e), .f(counterds_1_f), .g(counterds_1_g));
  _7_Segment_Display u_7_segment_display_3 (
    .g(counterds_1_g), .f(counterds_1_f), .a(counterds_1_a), .b(counterds_1_b), .e(counterds_1_e),
    .d(counterds_1_d), .c(counterds_1_c));  // open: dp

  // Notes on the sheet:
  //   Mood Changer
  //   Encoder
  //   Reset
  //   Set
  //   Mood
  //   Pass Matches
  //   Mood 2
  //   Counter
  //   Mood 1
  //   Password taken
  //   Counter Display
  //   MOOD -1:   Only display the digit
  //   Mood -2: save and compare
  //   5 digit password
  //   Counter 0-4= 5 digit
endmodule

module decoder (
  input  w,
  input  x,
  input  y,
  input  z,
  output A,
  output B,
  output C,
  output D,
  output E,
  output F,
  output G
);

  wire and_1_out, and_2_out, and_3_out, and_4_out, and_5_out, and_6_out, and_7_out, and_8_out, and_9_out,
       and_10_out, and_11_out, and_12_out, and_13_out, and_14_out, and_15_out, and_16_out, and_17_out,
       and_18_out, and_19_out, and_20_out, and_21_out, and_22_out, and_23_out, and_24_out, and_25_out,
       and_26_out, not_1_out, not_2_out, not_3_out, not_4_out, not_5_out, not_6_out, not_7_out, not_8_out,
       not_9_out, not_10_out, not_11_out, not_12_out, not_13_out, not_14_out, not_15_out, not_16_out,
       not_17_out, not_18_out, not_19_out, not_20_out, not_21_out, not_22_out, not_23_out, not_24_out,
       not_25_out, not_26_out, not_27_out, not_28_out, not_29_out, not_30_out, not_31_out, not_32_out,
       not_33_out, not_34_out, not_35_out, not_36_out, not_37_out, not_38_out, not_39_out;

  not not_1 (not_1_out, x);
  and and_1 (and_1_out, not_1_out, z);
  not not_2 (not_2_out, w);
  and and_2 (and_2_out, not_2_out, x, not_3_out);
  not not_3 (not_3_out, z);
  not not_4 (not_4_out, w);
  and and_3 (and_3_out, not_4_out, x, y);
  and and_4 (and_4_out, w, not_5_out);
  not not_5 (not_5_out, x);
  not not_6 (not_6_out, x);
  and and_5 (and_5_out, not_6_out, z);
  not not_7 (not_7_out, x);
  and and_6 (and_6_out, not_7_out, y);
  not not_8 (not_8_out, w);
  and and_7 (and_7_out, not_8_out, x, not_9_out);
  not not_9 (not_9_out, y);
  and and_8 (and_8_out, w, not_10_out);
  not not_10 (not_10_out, x);
  not not_11 (not_11_out, w);
  not not_12 (not_12_out, y);
  and and_9 (and_9_out, not_11_out, not_12_out, z);
  not not_13 (not_13_out, w);
  and and_10 (and_10_out, not_13_out, y, not_14_out);
  not not_14 (not_14_out, z);
  not not_15 (not_15_out, w);
  and and_11 (and_11_out, not_15_out, x);
  and and_12 (and_12_out, w, not_16_out);
  not not_16 (not_16_out, x);
  not not_17 (not_17_out, x);
  not not_18 (not_18_out, y);
  not not_19 (not_19_out, w);
  not not_20 (not_20_out, w);
  not not_21 (not_21_out, z);
  not not_22 (not_22_out, x);
  not not_23 (not_23_out, z);
  not not_24 (not_24_out, x);
  and and_13 (and_13_out, not_24_out, not_25_out, z);
  not not_25 (not_25_out, y);
  not not_26 (not_26_out, w);
  and and_14 (and_14_out, not_26_out, y, z);
  not not_27 (not_27_out, w);
  not not_28 (not_28_out, y);
  not not_29 (not_29_out, x);
  not not_30 (not_30_out, y);
  not not_31 (not_31_out, w);
  not not_32 (not_32_out, x);
  not not_33 (not_33_out, z);
  not not_34 (not_34_out, w);
  not not_35 (not_35_out, w);
  not not_36 (not_36_out, x);
  not not_37 (not_37_out, y);
  not not_38 (not_38_out, x);
  not not_39 (not_39_out, z);
  or or_1 (A, and_1_out, and_2_out, and_3_out, and_4_out);
  or or_2 (B, and_5_out, and_6_out, and_7_out, and_8_out);
  or or_3 (C, and_9_out, and_10_out, and_11_out, and_12_out);
  and and_15 (and_15_out, not_17_out, not_18_out, z);
  and and_16 (and_16_out, not_19_out, y, z);
  and and_17 (and_17_out, not_20_out, x, not_21_out);
  and and_18 (and_18_out, w, not_22_out, y, not_23_out);
  or or_4 (E, and_13_out, and_14_out);
  and and_19 (and_19_out, not_27_out, not_28_out, z);
  and and_20 (and_20_out, not_29_out, not_30_out, z);
  and and_21 (and_21_out, not_31_out, x, y);
  and and_22 (and_22_out, w, not_32_out, y, not_33_out);
  and and_23 (and_23_out, not_34_out, y, z);
  and and_24 (and_24_out, not_35_out, x);
  and and_25 (and_25_out, w, not_36_out, not_37_out, z);
  and and_26 (and_26_out, w, not_38_out, y, not_39_out);
  or or_5 (D, and_15_out, and_16_out, and_17_out, and_18_out);
  or or_6 (F, and_19_out, and_20_out, and_21_out, and_22_out);
  or or_7 (G, and_23_out, and_24_out, and_25_out, and_26_out);
endmodule

module comparator (
  input  a1,
  input  b1,
  input  a2,
  input  b2,
  input  a3,
  input  b3,
  input  a4,
  input  b4,
  output out_9
);

  wire xnor_1_out, xnor_2_out, xnor_3_out, xnor_4_out;

  xnor xnor_1 (xnor_1_out, a1, b1);
  xnor xnor_2 (xnor_2_out, a2, b2);
  xnor xnor_3 (xnor_3_out, a3, b3);
  xnor xnor_4 (xnor_4_out, a4, b4);
  and and_1 (out_9, xnor_1_out, xnor_2_out, xnor_3_out, xnor_4_out);
endmodule

module encoderwithcontroler (
  input  _0,
  input  _1,
  input  _2,
  input  _3,
  input  _4,
  input  _5,
  input  _6,
  input  _7,
  input  _8,
  input  _9,
  output W,
  output X,
  output Y,
  output Z
);

  or or_1 (W, _9, _8, _7);
  or or_2 (X, _3, _4, _5, _6);
  or or_3 (Y, _1, _2, _5, _6, _9);
  or or_4 (Z, _0, _2, _4, _8, _6);
endmodule

module counter (
  input  a,
  input  b,
  input  c,
  output x,
  output y,
  output z
);

  wire and_1_out, and_2_out, and_3_out, and_4_out, and_5_out, and_6_out, not_1_out, not_2_out, not_3_out,
       not_4_out;

  and and_1 (and_1_out, b, c);
  not not_1 (not_1_out, b);
  not not_2 (not_2_out, c);
  not not_3 (not_3_out, a);
  not not_4 (not_4_out, c);
  or or_1 (x, and_1_out, a);
  and and_2 (and_2_out, not_1_out, c);
  and and_3 (and_3_out, b, not_2_out);
  and and_4 (and_4_out, a, b);
  and and_5 (and_5_out, not_3_out, not_4_out);
  and and_6 (and_6_out, a, b);
  or or_2 (y, and_2_out, and_3_out, and_4_out);
  or or_3 (z, and_5_out, and_6_out);
endmodule

module flip_flop (
  input  w,
  input  x,
  input  y,
  input  z,
  input  clr,
  input  set,
  input  C,
  output out_8,
  output out_9,
  output out_10,
  output out_11
);

  D_Flip_Flop d_ff_1 (.clk(C), .D(w), .Q(out_8), .en(set), .reset(clr));  // open: Qn, preset
  D_Flip_Flop d_ff_2 (.clk(C), .D(x), .Q(out_9), .en(set), .reset(clr));  // open: Qn, preset
  D_Flip_Flop d_ff_3 (.clk(C), .D(y), .Q(out_10), .en(set), .reset(clr));  // open: Qn, preset
  D_Flip_Flop d_ff_4 (.clk(C), .D(z), .Q(out_11), .en(set), .reset(clr));  // open: Qn, preset
endmodule

module ppp (
  input  A,
  input  B,
  input  C,
  output Da,
  output Db,
  output Dc
);

  wire and_1_out, and_2_out, and_3_out, and_4_out, and_5_out, and_6_out, not_1_out, not_2_out, not_3_out,
       not_5_out, not_6_out, or_2_out;

  not not_1 (not_1_out, A);
  not not_2 (not_2_out, B);
  not not_3 (not_3_out, C);
  not not_4 (Dc, C);
  and and_1 (and_1_out, not_1_out, B);
  not not_5 (not_5_out, B);
  and and_2 (and_2_out, not_2_out, C);
  and and_3 (and_3_out, B, not_3_out);
  and and_4 (and_4_out, and_1_out, C);
  and and_5 (and_5_out, A, not_5_out);
  not not_6 (not_6_out, C);
  or or_1 (Db, and_2_out, and_3_out);
  or or_2 (or_2_out, and_4_out, and_5_out);
  and and_6 (and_6_out, A, not_6_out);
  or or_3 (Da, or_2_out, and_6_out);
endmodule

module ct (
  input  E,
  input  C,
  input  R,
  output A,
  output B,
  output C_2
);

  wire and_4_out, d_ff_1_q, d_ff_2_q, d_ff_3_q, not_1_out, or_1_out, ppp_1_da, ppp_1_db, ppp_1_dc;

  and and_1 (A, E, d_ff_1_q);
  and and_2 (B, E, d_ff_2_q);
  and and_3 (C_2, d_ff_3_q, E);
  ppp ppp_1 (.A(d_ff_1_q), .B(d_ff_2_q), .C(d_ff_3_q), .Da(ppp_1_da), .Db(ppp_1_db), .Dc(ppp_1_dc));
  not not_1 (not_1_out, d_ff_2_q);
  D_Flip_Flop d_ff_1 (.clk(C), .D(ppp_1_da), .Q(d_ff_1_q), .reset(or_1_out));  // open: Qn, preset, en
  D_Flip_Flop d_ff_2 (.clk(C), .D(ppp_1_db), .Q(d_ff_2_q), .reset(or_1_out));  // open: Qn, preset, en
  D_Flip_Flop d_ff_3 (.clk(C), .D(ppp_1_dc), .Q(d_ff_3_q), .reset(or_1_out));  // open: Qn, preset, en
  and and_4 (and_4_out, d_ff_3_q, not_1_out, d_ff_1_q);
  or or_1 (or_1_out, and_4_out, R);
endmodule

module disC (
  input  A,
  input  B,
  input  C,
  output A1,
  output B1,
  output C1,
  output D1,
  output E1
);

  wire and_1_out, and_2_out, and_3_out, and_4_out, and_5_out, not_1_out, not_2_out, not_3_out, not_4_out,
       not_5_out, not_6_out, not_7_out, not_8_out;

  not not_1 (not_1_out, A);
  not not_2 (not_2_out, B);
  not not_3 (not_3_out, A);
  not not_4 (not_4_out, A);
  not not_5 (not_5_out, B);
  not not_6 (not_6_out, B);
  and and_1 (and_1_out, not_1_out, not_2_out);
  and and_2 (and_2_out, not_3_out, B);
  not not_7 (not_7_out, C);
  and and_3 (and_3_out, not_4_out, B);
  and and_4 (and_4_out, A, not_5_out);
  not not_8 (not_8_out, C);
  and and_5 (and_5_out, A, not_6_out);
  and and_6 (A1, and_1_out, C);
  and and_7 (B1, and_2_out, not_7_out);
  and and_8 (C1, and_3_out, C);
  and and_9 (D1, and_4_out, not_8_out);
  and and_10 (E1, and_5_out, C);
endmodule

module plk (
  input  w,
  input  x,
  input  y,
  input  z,
  input  clr,
  input  set,
  output chk,
  output clk,
  output Sled
);

  wire comparator_1_out_9, comparator_2_out_9, comparator_3_out_9, comparator_4_out_9, comparator_5_out_9,
       ct_1_a, ct_1_b, ct_1_c_2, ct_2_a, ct_2_b, ct_2_c_2, d_ff_1_qn, disc_1_a1, disc_1_b1, disc_1_c1,
       disc_1_d1, disc_1_e1, disc_2_a1, disc_2_b1, disc_2_c1, disc_2_d1, disc_2_e1, flip_flop_1_out_8,
       flip_flop_1_out_9, flip_flop_1_out_10, flip_flop_1_out_11, flip_flop_2_out_8, flip_flop_2_out_9,
       flip_flop_2_out_10, flip_flop_2_out_11, flip_flop_3_out_8, flip_flop_3_out_9, flip_flop_3_out_10,
       flip_flop_3_out_11, flip_flop_4_out_8, flip_flop_4_out_9, flip_flop_4_out_10, flip_flop_4_out_11,
       flip_flop_5_out_8, flip_flop_5_out_9, flip_flop_5_out_10, flip_flop_5_out_11, flip_flop_6_out_8,
       flip_flop_6_out_9, flip_flop_6_out_10, flip_flop_6_out_11, flip_flop_7_out_8, flip_flop_7_out_9,
       flip_flop_7_out_10, flip_flop_7_out_11, flip_flop_8_out_8, flip_flop_8_out_9, flip_flop_8_out_10,
       flip_flop_8_out_11, flip_flop_9_out_8, flip_flop_9_out_9, flip_flop_9_out_10, flip_flop_9_out_11,
       flip_flop_10_out_8, flip_flop_10_out_9, flip_flop_10_out_10, flip_flop_10_out_11, not_1_out;

  D_Flip_Flop d_ff_1 (.clk(set), .D(d_ff_1_qn), .Q(Sled), .Qn(d_ff_1_qn));  // open: preset, en, reset
  or or_1 (clk, z, y, x, w);
  ct ct_1 (.E(Sled), .A(ct_1_a), .B(ct_1_b), .C_2(ct_1_c_2), .C(clk), .R(clr));
  disC disc_1 (
    .A(ct_1_a), .B(ct_1_b), .C(ct_1_c_2), .A1(disc_1_a1), .B1(disc_1_b1), .C1(disc_1_c1), .D1(disc_1_d1),
    .E1(disc_1_e1));
  flip_flop flip_flop_1 (
    .w(w), .x(x), .y(y), .z(z), .clr(clr), .set(Sled), .C(disc_1_e1), .out_8(flip_flop_1_out_8),
    .out_9(flip_flop_1_out_9), .out_10(flip_flop_1_out_10), .out_11(flip_flop_1_out_11));
  flip_flop flip_flop_2 (
    .w(w), .x(x), .y(y), .z(z), .clr(clr), .set(Sled), .C(disc_1_d1), .out_8(flip_flop_2_out_8),
    .out_9(flip_flop_2_out_9), .out_10(flip_flop_2_out_10), .out_11(flip_flop_2_out_11));
  flip_flop flip_flop_3 (
    .w(w), .x(x), .y(y), .z(z), .clr(clr), .set(Sled), .C(disc_1_c1), .out_8(flip_flop_3_out_8),
    .out_9(flip_flop_3_out_9), .out_10(flip_flop_3_out_10), .out_11(flip_flop_3_out_11));
  comparator comparator_1 (
    .a1(flip_flop_1_out_11), .a2(flip_flop_1_out_10), .a3(flip_flop_1_out_9), .a4(flip_flop_1_out_8),
    .out_9(comparator_1_out_9), .b1(flip_flop_6_out_11), .b2(flip_flop_6_out_10), .b3(flip_flop_6_out_9),
    .b4(flip_flop_6_out_8));
  flip_flop flip_flop_4 (
    .w(w), .x(x), .y(y), .z(z), .clr(clr), .set(Sled), .C(disc_1_b1), .out_8(flip_flop_4_out_8),
    .out_9(flip_flop_4_out_9), .out_10(flip_flop_4_out_10), .out_11(flip_flop_4_out_11));
  flip_flop flip_flop_5 (
    .w(w), .x(x), .y(y), .z(z), .clr(clr), .set(Sled), .C(disc_1_a1), .out_8(flip_flop_5_out_8),
    .out_9(flip_flop_5_out_9), .out_10(flip_flop_5_out_10), .out_11(flip_flop_5_out_11));
  comparator comparator_2 (
    .a1(flip_flop_2_out_11), .a2(flip_flop_2_out_10), .a3(flip_flop_2_out_9), .a4(flip_flop_2_out_8),
    .out_9(comparator_2_out_9), .b1(flip_flop_7_out_11), .b2(flip_flop_7_out_10), .b3(flip_flop_7_out_9),
    .b4(flip_flop_7_out_8));
  not not_1 (not_1_out, Sled);
  ct ct_2 (.E(not_1_out), .A(ct_2_a), .B(ct_2_b), .C_2(ct_2_c_2), .C(clk), .R(clr));
  disC disc_2 (
    .A(ct_2_a), .B(ct_2_b), .C(ct_2_c_2), .A1(disc_2_a1), .B1(disc_2_b1), .C1(disc_2_c1), .D1(disc_2_d1),
    .E1(disc_2_e1));
  comparator comparator_3 (
    .a1(flip_flop_3_out_11), .a2(flip_flop_3_out_10), .a3(flip_flop_3_out_9), .a4(flip_flop_3_out_8),
    .out_9(comparator_3_out_9), .b1(flip_flop_8_out_11), .b2(flip_flop_8_out_10), .b3(flip_flop_8_out_9),
    .b4(flip_flop_8_out_8));
  flip_flop flip_flop_6 (
    .w(w), .x(x), .y(y), .z(z), .clr(clr), .set(not_1_out), .C(disc_2_e1), .out_8(flip_flop_6_out_8),
    .out_9(flip_flop_6_out_9), .out_10(flip_flop_6_out_10), .out_11(flip_flop_6_out_11));
  flip_flop flip_flop_7 (
    .w(w), .x(x), .y(y), .z(z), .clr(clr), .set(not_1_out), .C(disc_2_d1), .out_8(flip_flop_7_out_8),
    .out_9(flip_flop_7_out_9), .out_10(flip_flop_7_out_10), .out_11(flip_flop_7_out_11));
  comparator comparator_4 (
    .a1(flip_flop_9_out_11), .a2(flip_flop_4_out_10), .a3(flip_flop_4_out_9), .a4(flip_flop_4_out_8),
    .out_9(comparator_4_out_9), .b1(flip_flop_4_out_11), .b2(flip_flop_9_out_10), .b3(flip_flop_9_out_9),
    .b4(flip_flop_9_out_8));
  flip_flop flip_flop_8 (
    .w(w), .x(x), .y(y), .z(z), .clr(clr), .set(not_1_out), .C(disc_2_c1), .out_8(flip_flop_8_out_8),
    .out_9(flip_flop_8_out_9), .out_10(flip_flop_8_out_10), .out_11(flip_flop_8_out_11));
  flip_flop flip_flop_9 (
    .w(w), .x(x), .y(y), .z(z), .clr(clr), .set(not_1_out), .C(disc_2_b1), .out_8(flip_flop_9_out_8),
    .out_9(flip_flop_9_out_9), .out_10(flip_flop_9_out_10), .out_11(flip_flop_9_out_11));
  and and_1 (chk, comparator_5_out_9, comparator_4_out_9, comparator_3_out_9, comparator_2_out_9, comparator_1_out_9);
  comparator comparator_5 (
    .a1(flip_flop_10_out_11), .a2(flip_flop_10_out_10), .a3(flip_flop_10_out_9), .a4(flip_flop_10_out_8),
    .out_9(comparator_5_out_9), .b1(flip_flop_5_out_11), .b2(flip_flop_5_out_10), .b3(flip_flop_5_out_9),
    .b4(flip_flop_5_out_8));
  flip_flop flip_flop_10 (
    .w(w), .x(x), .y(y), .z(z), .clr(clr), .set(not_1_out), .C(disc_2_a1), .out_8(flip_flop_10_out_8),
    .out_9(flip_flop_10_out_9), .out_10(flip_flop_10_out_10), .out_11(flip_flop_10_out_11));
endmodule

module counterDs (
  input  in_1,
  input  Y,
  input  Z,
  output a,
  output b,
  output c,
  output d,
  output e,
  output f,
  output g
);

  wire and_1_out, and_2_out, and_3_out, and_4_out, and_5_out, and_6_out, and_7_out, and_10_out, and_11_out,
       not_1_out, not_2_out, not_3_out, not_4_out, not_5_out, not_6_out, not_7_out, not_8_out, not_9_out,
       not_10_out, not_11_out, not_12_out, not_13_out, not_14_out, not_15_out, not_16_out, not_17_out,
       not_18_out, not_19_out;

  not not_1 (not_1_out, in_1);
  not not_2 (not_2_out, Z);
  not not_3 (not_3_out, in_1);
  not not_4 (not_4_out, Y);
  not not_5 (not_5_out, Z);
  not not_6 (not_6_out, Y);
  not not_7 (not_7_out, Z);
  not not_8 (not_8_out, in_1);
  not not_9 (not_9_out, in_1);
  not not_10 (not_10_out, Z);
  not not_11 (not_11_out, in_1);
  not not_12 (not_12_out, in_1);
  not not_13 (not_13_out, Z);
  not not_14 (not_14_out, Y);
  not not_15 (not_15_out, Z);
  not not_16 (not_16_out, in_1);
  not not_17 (not_17_out, Y);
  not not_18 (not_18_out, Z);
  and and_1 (and_1_out, not_1_out, not_2_out);
  and and_2 (and_2_out, not_3_out, Y);
  not not_19 (not_19_out, in_1);
  and and_3 (and_3_out, not_4_out, not_5_out);
  and and_4 (and_4_out, not_6_out, not_7_out);
  and and_5 (and_5_out, not_8_out, Z);
  and and_6 (and_6_out, not_9_out, not_10_out);
  and and_7 (and_7_out, not_11_out, Y);
  and and_8 (e, not_12_out, not_13_out);
  and and_9 (f, not_14_out, not_15_out);
  and and_10 (and_10_out, not_16_out, Y);
  and and_11 (and_11_out, in_1, not_17_out, not_18_out);
  or or_1 (a, and_1_out, and_2_out);
  or or_2 (b, not_19_out, and_3_out);
  or or_3 (c, and_4_out, and_5_out);
  or or_4 (d, and_6_out, and_7_out);
  or or_5 (g, and_10_out, and_11_out);
endmodule

module cccccooo (
  input  C,
  input  R,
  input  in_3,
  output A,
  output B,
  output C_2
);

  wire and_1_out, nor_1_out, not_1_out, not_2_out, or_1_out, ppp_1_da, ppp_1_db, ppp_1_dc;

  not not_1 (not_1_out, in_3);
  ppp ppp_1 (.A(A), .B(B), .C(C_2), .Da(ppp_1_da), .Db(ppp_1_db), .Dc(ppp_1_dc));
  not not_2 (not_2_out, B);
  nor nor_1 (nor_1_out, not_1_out, in_3);
  D_Flip_Flop d_ff_1 (.clk(C), .D(ppp_1_da), .Q(A), .reset(or_1_out));  // open: Qn, preset, en
  D_Flip_Flop d_ff_2 (.clk(C), .D(ppp_1_db), .Q(B), .reset(or_1_out));  // open: Qn, preset, en
  D_Flip_Flop d_ff_3 (.clk(C), .D(ppp_1_dc), .Q(C_2), .reset(or_1_out));  // open: Qn, preset, en
  and and_1 (and_1_out, C_2, not_2_out, A);
  or or_1 (or_1_out, and_1_out, nor_1_out, R);
endmodule

module mood (
  input  w,
  input  x,
  input  y,
  input  z,
  input  Mood,
  input  clr,
  input  Set,
  output chk,
  output clk,
  output Sled,
  output OFFLED,
  output ON_LED
);

  wire and_1_out, and_2_out, and_3_out, and_4_out, d_ff_1_qn;

  D_Flip_Flop d_ff_1 (.clk(Mood), .D(d_ff_1_qn), .Q(ON_LED), .Qn(d_ff_1_qn));  // open: preset, en, reset
  and and_1 (and_1_out, w, ON_LED);
  and and_2 (and_2_out, x, ON_LED);
  and and_3 (and_3_out, y, ON_LED);
  and and_4 (and_4_out, ON_LED, z);
  plk plk_1 (
    .w(and_1_out), .x(and_2_out), .y(and_3_out), .z(and_4_out), .clr(clr), .set(Set), .chk(chk), .clk(clk),
    .Sled(Sled));
  not not_1 (OFFLED, ON_LED);
endmodule
